// Logisim project 19101284.circ as structural Verilog: 10 circuits, main circuit main
module main (
);

  wire clock_1_out, oneoftwodecoder_1_y0, oneoftwodecoder_1_y1, oneoftwodecoder_1_y2, oneoftwodecoder_1_y3;
  wire [1:0] twobitcounter_1_d;
  wire [15:0] controlled_buffer_1_out, controlled_buffer_1_out_2, controlled_buffer_1_out_3,
       controlled_buffer_1_out_4, controlled_buffer_2_out_2, controlled_buffer_2_out_3,
       controlled_buffer_5_out, controlled_buffer_5_out_2, controlled_buffer_5_out_3,
       controlled_buffer_5_out_4, controlled_buffer_6_out, controlled_buffer_6_out_2,
       controlled_buffer_6_out_3, controlled_buffer_6_out_4, controlled_buffer_7_out,
       controlled_buffer_7_out_2, controlled_buffer_7_out_3, controlled_buffer_7_out_4,
       controlled_buffer_8_out, controlled_buffer_8_out_2, controlled_buffer_8_out_3,
       controlled_buffer_8_out_4, controlled_buffer_11_out, controlled_buffer_11_out_2,
       controlled_buffer_11_out_3, controlled_buffer_11_out_4, controlled_buffer_12_out,
       controlled_buffer_12_out_2, controlled_buffer_12_out_3, controlled_buffer_12_out_4;
  wire [31:0] controlled_buffer_2_out;
  wire [63:0] channel_1_l1, channel_1_l2, channel_1_l3, channel_1_l4, controlled_buffer_3_out,
       controlled_buffer_4_out, controlled_buffer_9_out, controlled_buffer_10_out, controlled_buffer_13_out,
       controlled_buffer_14_out, controlled_buffer_15_out, controlled_buffer_16_out;

  Clock clock_1 (.out(clock_1_out));
  Multiplexer #(.select(2), .width(64)) multiplexer_1 ();  // open: in0, in1, in2, in3, out, sel
  TwoBitCounter twobitcounter_1 (.CLK(clock_1_out), .D(twobitcounter_1_d));
  Hex_Digit_Display #(.decimalPoint("false")) hex_digit_display_1 (.value({2'b00, twobitcounter_1_d}));
  Channel channel_1 (
    .S0(twobitcounter_1_d[0]), .S1(twobitcounter_1_d[1]), .L1(channel_1_l1), .L2(channel_1_l2),
    .L3(channel_1_l3), .L4(channel_1_l4));
  OneOfTwoDecoder oneoftwodecoder_1 (
    .A(twobitcounter_1_d[0]), .B(twobitcounter_1_d[1]), .Y0(oneoftwodecoder_1_y0), .Y1(oneoftwodecoder_1_y1),
    .Y2(oneoftwodecoder_1_y2), .Y3(oneoftwodecoder_1_y3));
  assign {controlled_buffer_1_out_4, controlled_buffer_1_out_3, controlled_buffer_1_out_2, controlled_buffer_1_out} = oneoftwodecoder_1_y3 ? channel_1_l1 : 64'bz;  // Controlled_Buffer controlled_buffer_1
  DotMatrix #(.matrixcols(16), .matrixrows(16)) dotmatrix_1 (
    .col0(controlled_buffer_1_out_4), .col1(controlled_buffer_1_out_3), .col2(controlled_buffer_1_out_2),
    .col3(controlled_buffer_1_out), .col4(controlled_buffer_2_out_3), .col5(controlled_buffer_2_out_2),
    .col6(controlled_buffer_2_out[31:16]), .col7(controlled_buffer_2_out[15:0]),
    .col8(controlled_buffer_3_out[63:48]), .col9(controlled_buffer_3_out[47:32]),
    .col10(controlled_buffer_3_out[31:16]), .col11(controlled_buffer_3_out[15:0]),
    .col12(controlled_buffer_4_out[63:48]), .col13(controlled_buffer_4_out[47:32]),
    .col14(controlled_buffer_4_out[31:16]), .col15(controlled_buffer_4_out[15:0]));
  assign {controlled_buffer_2_out_3, controlled_buffer_2_out_2, controlled_buffer_2_out} = oneoftwodecoder_1_y3 ? channel_1_l2 : 64'bz;  // Controlled_Buffer controlled_buffer_2
  assign controlled_buffer_3_out = oneoftwodecoder_1_y3 ? channel_1_l3 : 64'bz;  // Controlled_Buffer controlled_buffer_3
  assign controlled_buffer_4_out = oneoftwodecoder_1_y3 ? channel_1_l4 : 64'bz;  // Controlled_Buffer controlled_buffer_4
  assign {controlled_buffer_5_out_4, controlled_buffer_5_out_3, controlled_buffer_5_out_2, controlled_buffer_5_out} = oneoftwodecoder_1_y2 ? channel_1_l1 : 64'bz;  // Controlled_Buffer controlled_buffer_5
  assign {controlled_buffer_6_out_4, controlled_buffer_6_out_3, controlled_buffer_6_out_2, controlled_buffer_6_out} = oneoftwodecoder_1_y2 ? channel_1_l2 : 64'bz;  // Controlled_Buffer controlled_buffer_6
  assign {controlled_buffer_7_out_4, controlled_buffer_7_out_3, controlled_buffer_7_out_2, controlled_buffer_7_out} = oneoftwodecoder_1_y2 ? channel_1_l3 : 64'bz;  // Controlled_Buffer controlled_buffer_7
  assign {controlled_buffer_8_out_4, controlled_buffer_8_out_3, controlled_buffer_8_out_2, controlled_buffer_8_out} = oneoftwodecoder_1_y2 ? channel_1_l4 : 64'bz;  // Controlled_Buffer controlled_buffer_8
  Hex_Digit_Display Volume ();  // open: value, dp
  Hex_Digit_Display CH ();  // open: value, dp
  assign controlled_buffer_9_out = oneoftwodecoder_1_y1 ? channel_1_l3 : 64'bz;  // Controlled_Buffer controlled_buffer_9
  assign controlled_buffer_10_out = oneoftwodecoder_1_y1 ? channel_1_l4 : 64'bz;  // Controlled_Buffer controlled_buffer_10
  assign {controlled_buffer_11_out_4, controlled_buffer_11_out_3, controlled_buffer_11_out_2, controlled_buffer_11_out} = oneoftwodecoder_1_y1 ? channel_1_l1 : 64'bz;  // Controlled_Buffer controlled_buffer_11
  assign {controlled_buffer_12_out_4, controlled_buffer_12_out_3, controlled_buffer_12_out_2, controlled_buffer_12_out} = oneoftwodecoder_1_y1 ? channel_1_l2 : 64'bz;  // Controlled_Buffer controlled_buffer_12
  DotMatrix #(.matrixcols(16), .matrixrows(16)) dotmatrix_2 (
    .col0(controlled_buffer_5_out_4), .col1(controlled_buffer_5_out_3), .col2(controlled_buffer_5_out_2),
    .col3(controlled_buffer_5_out), .col4(controlled_buffer_6_out_4), .col5(controlled_buffer_6_out_3),
    .col6(controlled_buffer_6_out_2), .col7(controlled_buffer_6_out), .col8(controlled_buffer_7_out_4),
    .col9(controlled_buffer_7_out_3), .col10(controlled_buffer_7_out_2), .col11(controlled_buffer_7_out),
    .col12(controlled_buffer_8_out_4), .col13(controlled_buffer_8_out_3), .col14(controlled_buffer_8_out_2),
    .col15(controlled_buffer_8_out));
  assign controlled_buffer_13_out = oneoftwodecoder_1_y0 ? channel_1_l1 : 64'bz;  // Controlled_Buffer controlled_buffer_13
  assign controlled_buffer_14_out = oneoftwodecoder_1_y0 ? channel_1_l2 : 64'bz;  // Controlled_Buffer controlled_buffer_14
  assign controlled_buffer_15_out = oneoftwodecoder_1_y0 ? channel_1_l3 : 64'bz;  // Controlled_Buffer controlled_buffer_15
  assign controlled_buffer_16_out = oneoftwodecoder_1_y0 ? channel_1_l4 : 64'bz;  // Controlled_Buffer controlled_buffer_16
  DotMatrix #(.matrixcols(16), .matrixrows(16)) dotmatrix_3 (
    .col0(controlled_buffer_11_out_4), .col1(controlled_buffer_11_out_3), .col2(controlled_buffer_11_out_2),
    .col3(controlled_buffer_11_out), .col4(controlled_buffer_12_out_4), .col5(controlled_buffer_12_out_3),
    .col6(controlled_buffer_12_out_2), .col7(controlled_buffer_12_out),
    .col8(controlled_buffer_9_out[63:48]), .col9(controlled_buffer_9_out[47:32]),
    .col10(controlled_buffer_9_out[31:16]), .col11(controlled_buffer_9_out[15:0]),
    .col12(controlled_buffer_10_out[63:48]), .col13(controlled_buffer_10_out[47:32]),
    .col14(controlled_buffer_10_out[31:16]), .col15(controlled_buffer_10_out[15:0]));
  DotMatrix #(.matrixcols(16), .matrixrows(16)) dotmatrix_4 (
    .col0(controlled_buffer_13_out[63:48]), .col1(controlled_buffer_13_out[47:32]),
    .col2(controlled_buffer_13_out[31:16]), .col3(controlled_buffer_13_out[15:0]),
    .col4(controlled_buffer_14_out[63:48]), .col5(controlled_buffer_14_out[47:32]),
    .col6(controlled_buffer_14_out[31:16]), .col7(controlled_buffer_14_out[15:0]),
    .col8(controlled_buffer_15_out[63:48]), .col9(controlled_buffer_15_out[47:32]),
    .col10(controlled_buffer_15_out[31:16]), .col11(controlled_buffer_15_out[15:0]),
    .col12(controlled_buffer_16_out[63:48]), .col13(controlled_buffer_16_out[47:32]),
    .col14(controlled_buffer_16_out[31:16]), .col15(controlled_buffer_16_out[15:0]));
endmodule

module HalfAdder (
  input  A,
  input  B,
  output S,
  output C
);

  xor xor_1 (S, A, B);
  and and_1 (C, A, B);
endmodule

module FullAdder (
  input  A,
  input  B,
  input  C_in,
  output S,
  output C_out
);

  wire halfadder_1_c, halfadder_1_s, halfadder_2_c;

  HalfAdder halfadder_1 (.A(A), .B(B), .S(halfadder_1_s), .C(halfadder_1_c));
  HalfAdder halfadder_2 (.A(halfadder_1_s), .B(C_in), .S(S), .C(halfadder_2_c));
  or or_1 (C_out, halfadder_1_c, halfadder_2_c);
endmodule

module MyCounter (
  input  CLK,
  output [7:0] D
);

  wire and_1_out, and_2_out, and_3_out, and_4_out, and_5_out, and_6_out;

  J_K_Flip_Flop j_k_ff_1 (.J(1'b1), .K(1'b1), .clk(CLK), .Q(D[0]));  // open: Qn, preset, reset
  J_K_Flip_Flop j_k_ff_2 (.J(D[0]), .K(D[0]), .clk(CLK), .Q(D[1]));  // open: Qn, preset, reset
  and and_1 (and_1_out, D[0], D[1]);
  J_K_Flip_Flop j_k_ff_3 (.J(and_1_out), .K(and_1_out), .clk(CLK), .Q(D[2]));  // open: Qn, preset, reset
  and and_2 (and_2_out, and_1_out, D[2]);
  J_K_Flip_Flop j_k_ff_4 (.J(and_2_out), .K(and_2_out), .clk(CLK), .Q(D[3]));  // open: Qn, preset, reset
  and and_3 (and_3_out, and_2_out, D[3]);
  J_K_Flip_Flop j_k_ff_5 (.J(and_3_out), .K(and_3_out), .clk(CLK), .Q(D[4]));  // open: Qn, preset, reset
  and and_4 (and_4_out, and_3_out, D[4]);
  J_K_Flip_Flop j_k_ff_6 (.J(and_4_out), .K(and_4_out), .clk(CLK), .Q(D[5]));  // open: Qn, preset, reset
  and and_5 (and_5_out, and_4_out, D[5]);
  J_K_Flip_Flop j_k_ff_7 (.J(and_5_out), .K(and_5_out), .clk(CLK), .Q(D[6]));  // open: Qn, preset, reset
  and and_6 (and_6_out, and_5_out, D[6]);
  J_K_Flip_Flop j_k_ff_8 (.J(and_6_out), .K(and_6_out), .clk(CLK), .Q(D[7]));  // open: Qn, preset, reset
endmodule

module EightBitAdder (
  input  [7:0] A,
  input  [7:0] B,
  output [7:0] S,
  output OVR
);

  wire fulladder_1_c_out, fulladder_2_c_out, fulladder_3_c_out, fulladder_4_c_out, fulladder_5_c_out,
       fulladder_6_c_out, fulladder_7_c_out;

  FullAdder fulladder_1 (.A(A[0]), .B(B[0]), .C_in(1'b0), .S(S[0]), .C_out(fulladder_1_c_out));
  FullAdder fulladder_2 (.A(A[1]), .B(B[1]), .C_in(fulladder_1_c_out), .S(S[1]), .C_out(fulladder_2_c_out));
  FullAdder fulladder_3 (.A(A[2]), .B(B[2]), .C_in(fulladder_2_c_out), .S(S[2]), .C_out(fulladder_3_c_out));
  FullAdder fulladder_4 (.A(A[3]), .B(B[3]), .C_in(fulladder_3_c_out), .S(S[3]), .C_out(fulladder_4_c_out));
  FullAdder fulladder_5 (.A(A[4]), .B(B[4]), .C_in(fulladder_4_c_out), .S(S[4]), .C_out(fulladder_5_c_out));
  FullAdder fulladder_6 (.A(A[5]), .B(B[5]), .C_in(fulladder_5_c_out), .S(S[5]), .C_out(fulladder_6_c_out));
  FullAdder fulladder_7 (.A(A[6]), .B(B[6]), .C_in(fulladder_6_c_out), .S(S[6]), .C_out(fulladder_7_c_out));
  FullAdder fulladder_8 (.A(A[7]), .B(B[7]), .C_in(fulladder_7_c_out), .S(S[7]), .C_out(OVR));
endmodule

module OneOfTwoDecoder (
  input  A,
  input  B,
  output Y0,
  output Y1,
  output Y2,
  output Y3
);

  wire not_1_out, not_2_out;

  not not_1 (not_1_out, A);
  not not_2 (not_2_out, B);
  and and_1 (Y0, not_1_out, not_2_out);
  and and_2 (Y1, A, not_2_out);
  and and_3 (Y2, not_1_out, B);
  and and_4 (Y3, A, B);

  // Notes on the sheet:
  //   OneOfTwoDecoder: Not
endmodule

module TwoBitCounter (
  input  CLK,
  output [1:0] D
);

  J_K_Flip_Flop j_k_ff_1 (.J(1'b1), .K(1'b1), .clk(CLK), .Q(D[0]));  // open: Qn, preset, reset
  J_K_Flip_Flop j_k_ff_2 (.J(D[0]), .K(D[0]), .clk(CLK), .Q(D[1]));  // open: Qn, preset, reset
endmodule

module LedMatrixSumulator (
  input  [7:0] in_1,
  input  [7:0] in_2,
  input  [7:0] in_3,
  input  [7:0] in_4,
  input  [7:0] in_5,
  input  [7:0] in_6,
  input  [7:0] in_7,
  input  [7:0] in_8,
  input  [7:0] in_9,
  input  [7:0] in_10,
  input  [7:0] in_11,
  input  [7:0] in_12,
  input  [7:0] in_13,
  input  [7:0] in_14,
  input  [7:0] in_15,
  input  [7:0] in_16,
  input  [7:0] in_17,
  input  [7:0] in_18,
  input  [7:0] in_19,
  input  [7:0] in_20,
  input  [7:0] in_21,
  input  [7:0] in_22,
  input  [7:0] in_23,
  input  [7:0] in_24,
  input  [7:0] in_25,
  input  [7:0] in_26,
  input  [7:0] in_27,
  input  [7:0] in_28,
  input  [7:0] in_29,
  input  [7:0] in_30,
  input  [7:0] in_31,
  input  [7:0] in_32,
  output [63:0] out_33,
  output [63:0] out_34,
  output [63:0] out_35,
  output [63:0] out_36
);

  DotMatrix #(.matrixcols(16), .matrixrows(16)) dotmatrix_1 (
    .col0({in_1, in_17}), .col1({in_2, in_18}), .col2({in_3, in_19}), .col3({in_4, in_20}),
    .col4({in_5, in_21}), .col5({in_6, in_22}), .col6({in_7, in_23}), .col7({in_8, in_24}),
    .col8({in_9, in_25}), .col9({in_10, in_26}), .col10({in_11, in_27}), .col11({in_12, in_28}),
    .col12({in_13, in_29}), .col13({in_14, in_30}), .col14({in_15, in_31}), .col15({in_16, in_32}));

  assign out_33 = {in_13, in_29, in_14, in_30, in_15, in_31, in_16, in_32};
  assign out_34 = {in_1, in_17, in_2, in_18, in_3, in_19, in_4, in_20};
  assign out_35 = {in_9, in_25, in_10, in_26, in_11, in_27, in_12, in_28};
  assign out_36 = {in_5, in_21, in_6, in_22, in_7, in_23, in_8, in_24};
endmodule

module Channel (
  input  S0,
  input  S1,
  output [63:0] L1,
  output [63:0] L2,
  output [63:0] L3,
  output [63:0] L4
);

  BusDriver busdriver_1 (
    .D3(64'h10f810047006), .D2(64'h5002538253925012), .D1(64'h5012539253825002), .D0(64'h7006100410f80000),
    .C3(64'h70009003303c2), .C2(64'hc34080810181024), .C1(64'h1044108831084a10), .C0(64'h4c609b80a000c000),
    .B3(64'h2080208061c04143), .B2(64'h404e403040600f83), .B1(64'h103c20e049008880),
    .B0(64'hc87838070fc0083e), .A3(64'h102710251fe7002), .A2(64'h23ffe20022002), .A1(64'h3ffe010401040ffc),
    .A0(64'h41ffc10041004), .S0(S0), .S1(S1), .L1(L1), .L2(L2), .L3(L3), .L4(L4));
  DotMatrix #(.matrixcols(16), .matrixrows(16)) dotmatrix_1 (
    .col0(L1[63:48]), .col1(L1[47:32]), .col2(L1[31:16]), .col3(L1[15:0]), .col4(L2[63:48]),
    .col5(L2[47:32]), .col6(L2[31:16]), .col7(L2[15:0]), .col8(L3[63:48]), .col9(L3[47:32]),
    .col10(L3[31:16]), .col11(L3[15:0]), .col12(L4[63:48]), .col13(L4[47:32]), .col14(L4[31:16]),
    .col15(L4[15:0]));
endmodule

module BusDriver (
  input  [63:0] D3,
  input  [63:0] D2,
  input  [63:0] D1,
  input  [63:0] D0,
  input  [63:0] C3,
  input  [63:0] C2,
  input  [63:0] C1,
  input  [63:0] C0,
  input  [63:0] B3,
  input  [63:0] B2,
  input  [63:0] B1,
  input  [63:0] B0,
  input  [63:0] A3,
  input  [63:0] A2,
  input  [63:0] A1,
  input  [63:0] A0,
  input  S0,
  input  S1,
  output [63:0] L1,
  output [63:0] L2,
  output [63:0] L3,
  output [63:0] L4
);

  wire oneoftwodecoder_1_y0, oneoftwodecoder_1_y1, oneoftwodecoder_1_y2, oneoftwodecoder_1_y3;

  OneOfTwoDecoder oneoftwodecoder_1 (
    .A(S0), .B(S1), .Y0(oneoftwodecoder_1_y0), .Y1(oneoftwodecoder_1_y1), .Y2(oneoftwodecoder_1_y2),
    .Y3(oneoftwodecoder_1_y3));
  assign L1 = oneoftwodecoder_1_y3 ? D3 : 64'bz;  // Controlled_Buffer controlled_buffer_1
  assign L1 = oneoftwodecoder_1_y0 ? A3 : 64'bz;  // Controlled_Buffer controlled_buffer_2
  assign L1 = oneoftwodecoder_1_y1 ? B3 : 64'bz;  // Controlled_Buffer controlled_buffer_3
  assign L1 = oneoftwodecoder_1_y2 ? C3 : 64'bz;  // Controlled_Buffer controlled_buffer_4
  assign L2 = oneoftwodecoder_1_y3 ? D2 : 64'bz;  // Controlled_Buffer controlled_buffer_5
  assign L2 = oneoftwodecoder_1_y0 ? A2 : 64'bz;  // Controlled_Buffer controlled_buffer_6
  assign L2 = oneoftwodecoder_1_y1 ? B2 : 64'bz;  // Controlled_Buffer controlled_buffer_7
  assign L2 = oneoftwodecoder_1_y2 ? C2 : 64'bz;  // Controlled_Buffer controlled_buffer_8
  assign L3 = oneoftwodecoder_1_y3 ? D1 : 64'bz;  // Controlled_Buffer controlled_buffer_9
  assign L3 = oneoftwodecoder_1_y0 ? A1 : 64'bz;  // Controlled_Buffer controlled_buffer_10
  assign L3 = oneoftwodecoder_1_y1 ? B1 : 64'bz;  // Controlled_Buffer controlled_buffer_11
  assign L3 = oneoftwodecoder_1_y2 ? C1 : 64'bz;  // Controlled_Buffer controlled_buffer_12
  assign L4 = oneoftwodecoder_1_y3 ? D0 : 64'bz;  // Controlled_Buffer controlled_buffer_13
  assign L4 = oneoftwodecoder_1_y0 ? A0 : 64'bz;  // Controlled_Buffer controlled_buffer_14
  assign L4 = oneoftwodecoder_1_y1 ? B0 : 64'bz;  // Controlled_Buffer controlled_buffer_15
  assign L4 = oneoftwodecoder_1_y2 ? C0 : 64'bz;  // Controlled_Buffer controlled_buffer_16
endmodule
